# Fritzing sketch RPiMotorControl (saved by Fritzing 1.0.7)
breadboards: 1

parts:
  DRV_1 = DRV 8825 Stepper Motor Carrier, High Current [part_number="DRV 8825"]
  A1 = Raspberry Pi 5
  J1 = Camdenboss CTB0158-2 [part_number=CTB0158-2 package=THT]
  M1 = Stepper Motor - Bipolar
  R1 = Resistor [tolerance=±1% resistance=1k package=THT]
  C1 = Electrolytic Capacitor [capacitance=0.1mF voltage=50V package="100 mil [THT, electrolytic]"]

nets:
  N1: DRV_1.ENABLE, A1.GPIO17, R1.Pin_1
  N2: DRV_1.MS1, A1.GPIO14
  N3: DRV_1.MS2, A1.GPIO15
  N4: DRV_1.MS3, A1.GPIO18
  3.3V: DRV_1.RESET, DRV_1.SLEEP, A1.3V3, R1.Pin_0
  N5: DRV_1.STEP, A1.GPIO21
  N6: DRV_1.DIRECTION, A1.GPIO20
  N7: DRV_1.VOLTAGE_ST/_MT, J1.terminal_1, C1.+
  N8: DRV_1.GROUND_ST/_MT, J1.terminal_2, C1.-
  N9: DRV_1.OUT_2B, M1.A
  N10: DRV_1.OUT_2A, M1.C
  N11: DRV_1.OUT_1A, M1.B
  N12: DRV_1.OUT_1B, M1.D
  GND: DRV_1.GROUND_LOG, A1.GND, J1.pin2
  12V: J1.pin1

custom parts:
  Raspberry Pi 5: The RPi5, a faster version of the awesome Raspberry Pi4B ARM Board with 40 pin gpio.
